// Logisim project mesm_6.circ as structural Verilog: 12 circuits, main circuit main
module main (
);

  wire clock_1_out, cpu_1_dbus_read, cpu_1_dbus_write, cpu_1_ibus_fetch, dram_1_dbus_done, irom_1_o_done,
       IRQ_out, RESET_out;
  wire [14:0] cpu_1_dbus_addr, cpu_1_ibus_addr;
  wire [23:0] cpu_1_dbus_odata_h, cpu_1_dbus_odata_l, dram_1_dbus_odata_h, dram_1_dbus_odata_l,
       irom_1_odata_h, irom_1_odata_l;

  Clock clock_1 (.out(clock_1_out));
  Button RESET (.out(RESET_out));
  Button IRQ (.out(IRQ_out));
  IROM irom_1 (
    .CLK(clock_1_out), .FETCH(cpu_1_ibus_fetch), .I_ADDR(cpu_1_ibus_addr), .ODATA_L(irom_1_odata_l),
    .ODATA_H(irom_1_odata_h), .O_DONE(irom_1_o_done));
  CPU cpu_1 (
    .CLK(clock_1_out), .RESET(RESET_out), .IRQ(IRQ_out), .IBUS_IDATA_L(irom_1_odata_l),
    .IBUS_IDATA_H(irom_1_odata_h), .IBUS_DONE(irom_1_o_done), .DBUS_IDATA_L(dram_1_dbus_odata_l),
    .DBUS_IDATA_H(dram_1_dbus_odata_h), .DBUS_DONE(dram_1_dbus_done), .IBUS_FETCH(cpu_1_ibus_fetch),
    .IBUS_ADDR(cpu_1_ibus_addr), .DBUS_READ(cpu_1_dbus_read), .DBUS_WRITE(cpu_1_dbus_write),
    .DBUS_ADDR(cpu_1_dbus_addr), .DBUS_ODATA_L(cpu_1_dbus_odata_l), .DBUS_ODATA_H(cpu_1_dbus_odata_h));
  DRAM dram_1 (
    .CLK(clock_1_out), .DBUS_READ(cpu_1_dbus_read), .DBUS_WRITE(cpu_1_dbus_write),
    .DBUS_ADDR(cpu_1_dbus_addr), .DBUS_IDATA_L(cpu_1_dbus_odata_l), .DBUS_IDATA_H(cpu_1_dbus_odata_h),
    .DBUS_DONE(dram_1_dbus_done), .DBUS_ODATA_L(dram_1_dbus_odata_l), .DBUS_ODATA_H(dram_1_dbus_odata_h));
endmodule

module U_addr_gen (
  input  clk,
  input  sel_j_add,
  input  c_active,
  input  [23:0] cmd,
  input  [14:0] C_in,
  input  decode,
  input  [14:0] M_j,
  input  [14:0] M_i,
  output [14:0] U_addr
);

  wire [14:0] adder_1_out, bit_extender_1_out, multiplexer_1_out, multiplexer_2_out, multiplexer_3_out,
       V_ADDR_q;

  assign bit_extender_1_out = {{2{cmd[18]}}, {cmd[18], cmd[11:0]}};  // Bit_Extender bit_extender_1
  Multiplexer #(.width(15), .enable("false")) multiplexer_1 (
    .in0(bit_extender_1_out), .in1(cmd[14:0]), .out(multiplexer_1_out), .sel(cmd[19]));
  Adder #(.width(15)) adder_1 (.a(multiplexer_1_out), .b(C_in), .out(adder_1_out));  // open: cin, cout
  Multiplexer #(.width(15), .enable("false")) multiplexer_2 (
    .in0(multiplexer_1_out), .in1(adder_1_out), .out(multiplexer_2_out), .sel(c_active));
  Register #(.width(15)) V_ADDR (.D(multiplexer_2_out), .en(decode), .clk(clk), .Q(V_ADDR_q), .clr(1'b0));
  Multiplexer #(.width(15), .enable("false")) multiplexer_3 (
    .in0(V_ADDR_q), .in1(M_j), .out(multiplexer_3_out), .sel(sel_j_add));
  Adder #(.width(15)) adder_2 (.a(multiplexer_3_out), .b(M_i), .out(U_addr));  // open: cin, cout

  // Notes on the sheet:
  //   op_addr
  //   C + op_addr
endmodule

module M_regs (
  input  clk,
  input  [1:0] sel_mr,
  input  [3:0] reg_ind,
  input  [3:0] imm,
  input  [14:0] V_addr,
  input  [14:0] U_addr,
  input  [1:0] sel_mw,
  input  w_m,
  input  [2:0] sel_md,
  input  [14:0] PC,
  input  [14:0] ACC,
  input  [14:0] M_i,
  input  [14:0] M_i_p1,
  input  [14:0] M_i_m1,
  output [14:0] RD1,
  output [14:0] RD2
);

  wire decoder_1_out1, decoder_1_out2, decoder_1_out3, decoder_1_out4, decoder_1_out5, decoder_1_out6,
       decoder_1_out7, decoder_1_out8, decoder_1_out9, decoder_1_out10, decoder_1_out11, decoder_1_out12,
       decoder_1_out13, decoder_1_out14, decoder_1_out15, decoder_2_out1, decoder_2_out2, decoder_2_out3,
       decoder_2_out4, decoder_2_out5, decoder_2_out6, decoder_2_out7, decoder_2_out8, decoder_2_out9,
       decoder_2_out10, decoder_2_out11, decoder_2_out12, decoder_2_out13, decoder_2_out14, decoder_2_out15,
       decoder_3_out1, decoder_3_out2, decoder_3_out3, decoder_3_out4, decoder_3_out5, decoder_3_out6,
       decoder_3_out7, decoder_3_out8, decoder_3_out9, decoder_3_out10, decoder_3_out11, decoder_3_out12,
       decoder_3_out13, decoder_3_out14, decoder_3_out15;
  wire [3:0] bit_extender_1_out, bit_extender_2_out, multiplexer_1_out, multiplexer_2_out;
  wire [14:0] M1_q, M2_q, M3_q, M4_q, M5_q, M6_q, M7_q, M8_q, M9_q, M10_q, M11_q, M12_q, M13_q, M14_q, M15_q,
       multiplexer_3_out;

  Bit_Extender #(.in_width(15), .out_width(4), .\type ("zero")) bit_extender_1 (.in(V_addr), .out(bit_extender_1_out));
  Bit_Extender #(.in_width(15), .out_width(4), .\type ("zero")) bit_extender_2 (.in(U_addr), .out(bit_extender_2_out));
  Multiplexer #(.select(2), .width(4)) multiplexer_1 (
    .in0(reg_ind), .in1(imm), .in2(bit_extender_1_out), .in3(bit_extender_2_out), .out(multiplexer_1_out),
    .sel(sel_mw), .en(w_m));
  Multiplexer #(.select(2), .width(4), .enable("false")) multiplexer_2 (
    .in0(reg_ind), .in1(imm), .in2(bit_extender_1_out), .in3(bit_extender_2_out), .out(multiplexer_2_out),
    .sel(sel_mr));
  Multiplexer #(.select(3), .width(15), .enable("false")) multiplexer_3 (
    .in0(PC), .in1(ACC), .in2(M_i), .in3(M_i_p1), .in4(M_i_m1), .in5(V_addr), .in6(U_addr),
    .out(multiplexer_3_out), .sel(sel_md));  // open: in7
  Decoder #(.select(4), .enable("false")) decoder_1 (
    .out1(decoder_1_out1), .out2(decoder_1_out2), .out3(decoder_1_out3), .out4(decoder_1_out4),
    .out5(decoder_1_out5), .out6(decoder_1_out6), .out7(decoder_1_out7), .out8(decoder_1_out8),
    .out9(decoder_1_out9), .out10(decoder_1_out10), .out11(decoder_1_out11), .out12(decoder_1_out12),
    .out13(decoder_1_out13), .out14(decoder_1_out14), .out15(decoder_1_out15), .sel(multiplexer_1_out));  // open: out0
  Register #(.width(15)) M1 (.D(multiplexer_3_out), .en(decoder_1_out1), .clk(clk), .Q(M1_q), .clr(1'b0));
  Register #(.width(15)) M2 (.D(multiplexer_3_out), .en(decoder_1_out2), .clk(clk), .Q(M2_q), .clr(1'b0));
  Register #(.width(15)) M3 (.D(multiplexer_3_out), .en(decoder_1_out3), .clk(clk), .Q(M3_q), .clr(1'b0));
  Register #(.width(15)) M4 (.D(multiplexer_3_out), .en(decoder_1_out4), .clk(clk), .Q(M4_q), .clr(1'b0));
  assign RD1 = decoder_2_out1 ? M1_q : 15'bz;  // Controlled_Buffer controlled_buffer_1
  assign RD2 = decoder_3_out1 ? M1_q : 15'bz;  // Controlled_Buffer controlled_buffer_2
  Decoder #(.select(4), .enable("false")) decoder_2 (
    .out1(decoder_2_out1), .out2(decoder_2_out2), .out3(decoder_2_out3), .out4(decoder_2_out4),
    .out5(decoder_2_out5), .out6(decoder_2_out6), .out7(decoder_2_out7), .out8(decoder_2_out8),
    .out9(decoder_2_out9), .out10(decoder_2_out10), .out11(decoder_2_out11), .out12(decoder_2_out12),
    .out13(decoder_2_out13), .out14(decoder_2_out14), .out15(decoder_2_out15), .sel(multiplexer_2_out));  // open: out0
  assign RD1 = decoder_2_out2 ? M2_q : 15'bz;  // Controlled_Buffer controlled_buffer_3
  assign RD2 = decoder_3_out2 ? M2_q : 15'bz;  // Controlled_Buffer controlled_buffer_4
  assign RD1 = decoder_2_out3 ? M3_q : 15'bz;  // Controlled_Buffer controlled_buffer_5
  assign RD2 = decoder_3_out3 ? M3_q : 15'bz;  // Controlled_Buffer controlled_buffer_6
  assign RD1 = decoder_2_out4 ? M4_q : 15'bz;  // Controlled_Buffer controlled_buffer_7
  assign RD2 = decoder_3_out4 ? M4_q : 15'bz;  // Controlled_Buffer controlled_buffer_8
  Decoder #(.select(4), .enable("false")) decoder_3 (
    .out1(decoder_3_out1), .out2(decoder_3_out2), .out3(decoder_3_out3), .out4(decoder_3_out4),
    .out5(decoder_3_out5), .out6(decoder_3_out6), .out7(decoder_3_out7), .out8(decoder_3_out8),
    .out9(decoder_3_out9), .out10(decoder_3_out10), .out11(decoder_3_out11), .out12(decoder_3_out12),
    .out13(decoder_3_out13), .out14(decoder_3_out14), .out15(decoder_3_out15), .sel(bit_extender_1_out));  // open: out0
  Register #(.width(15)) M5 (.D(multiplexer_3_out), .en(decoder_1_out5), .clk(clk), .Q(M5_q), .clr(1'b0));
  Register #(.width(15)) M6 (.D(multiplexer_3_out), .en(decoder_1_out6), .clk(clk), .Q(M6_q), .clr(1'b0));
  Register #(.width(15)) M7 (.D(multiplexer_3_out), .en(decoder_1_out7), .clk(clk), .Q(M7_q), .clr(1'b0));
  Register #(.width(15)) M8 (.D(multiplexer_3_out), .en(decoder_1_out8), .clk(clk), .Q(M8_q), .clr(1'b0));
  assign RD1 = decoder_2_out5 ? M5_q : 15'bz;  // Controlled_Buffer controlled_buffer_9
  assign RD2 = decoder_3_out5 ? M5_q : 15'bz;  // Controlled_Buffer controlled_buffer_10
  assign RD1 = decoder_2_out6 ? M6_q : 15'bz;  // Controlled_Buffer controlled_buffer_11
  assign RD2 = decoder_3_out6 ? M6_q : 15'bz;  // Controlled_Buffer controlled_buffer_12
  assign RD1 = decoder_2_out7 ? M7_q : 15'bz;  // Controlled_Buffer controlled_buffer_13
  assign RD2 = decoder_3_out7 ? M7_q : 15'bz;  // Controlled_Buffer controlled_buffer_14
  assign RD1 = decoder_2_out8 ? M8_q : 15'bz;  // Controlled_Buffer controlled_buffer_15
  assign RD2 = decoder_3_out8 ? M8_q : 15'bz;  // Controlled_Buffer controlled_buffer_16
  Register #(.width(15)) M9 (.D(multiplexer_3_out), .en(decoder_1_out9), .clk(clk), .Q(M9_q), .clr(1'b0));
  Register #(.width(15)) M10 (.D(multiplexer_3_out), .en(decoder_1_out10), .clk(clk), .Q(M10_q), .clr(1'b0));
  Register #(.width(15)) M11 (.D(multiplexer_3_out), .en(decoder_1_out11), .clk(clk), .Q(M11_q), .clr(1'b0));
  Register #(.width(15)) M12 (.D(multiplexer_3_out), .en(decoder_1_out12), .clk(clk), .Q(M12_q), .clr(1'b0));
  assign RD1 = decoder_2_out9 ? M9_q : 15'bz;  // Controlled_Buffer controlled_buffer_17
  assign RD2 = decoder_3_out9 ? M9_q : 15'bz;  // Controlled_Buffer controlled_buffer_18
  assign RD1 = decoder_2_out10 ? M10_q : 15'bz;  // Controlled_Buffer controlled_buffer_19
  assign RD2 = decoder_3_out10 ? M10_q : 15'bz;  // Controlled_Buffer controlled_buffer_20
  assign RD1 = decoder_2_out11 ? M11_q : 15'bz;  // Controlled_Buffer controlled_buffer_21
  assign RD2 = decoder_3_out11 ? M11_q : 15'bz;  // Controlled_Buffer controlled_buffer_22
  assign RD1 = decoder_2_out12 ? M12_q : 15'bz;  // Controlled_Buffer controlled_buffer_23
  assign RD2 = decoder_3_out12 ? M12_q : 15'bz;  // Controlled_Buffer controlled_buffer_24
  Register #(.width(15)) M13 (.D(multiplexer_3_out), .en(decoder_1_out13), .clk(clk), .Q(M13_q), .clr(1'b0));
  Register #(.width(15)) M14 (.D(multiplexer_3_out), .en(decoder_1_out14), .clk(clk), .Q(M14_q), .clr(1'b0));
  Register #(.width(15)) M15 (.D(multiplexer_3_out), .en(decoder_1_out15), .clk(clk), .Q(M15_q), .clr(1'b0));
  assign RD1 = decoder_2_out13 ? M13_q : 15'bz;  // Controlled_Buffer controlled_buffer_25
  assign RD2 = decoder_3_out13 ? M13_q : 15'bz;  // Controlled_Buffer controlled_buffer_26
  assign RD1 = decoder_2_out14 ? M14_q : 15'bz;  // Controlled_Buffer controlled_buffer_27
  assign RD2 = decoder_3_out14 ? M14_q : 15'bz;  // Controlled_Buffer controlled_buffer_28
  assign RD1 = decoder_2_out15 ? M15_q : 15'bz;  // Controlled_Buffer controlled_buffer_29
  assign RD2 = decoder_3_out15 ? M15_q : 15'bz;  // Controlled_Buffer controlled_buffer_30

  // Notes on the sheet:
  //   RA1
  //   RA2
  //   WA
endmodule

module ALU (
  input  CLK,
  input  [23:0] ALU_A_H,
  input  [23:0] ALU_A_L,
  input  [23:0] ALU_B_H,
  input  [23:0] ALU_B_L,
  input  [5:0] ALU_OP,
  output [23:0] ALU_R_H,
  output [23:0] ALU_R_L,
  output [23:0] ALU_Y_H,
  output [23:0] ALU_Y_L,
  output ALU_DONE
);


  assign ALU_DONE = 1'b0;
endmodule

module IROM (
  input  CLK,
  input  FETCH,
  input  [14:0] I_ADDR,
  output [23:0] ODATA_L,
  output [23:0] ODATA_H,
  output O_DONE
);

  wire and_1_out, not_1_out;
  wire [23:0] IROM_H_data, IROM_L_data;

  ROM #(.addrWidth(15), .dataWidth(24)) IROM_L (.addr(I_ADDR), .data(IROM_L_data));
  Register #(.width(1)) register_1 (.D(FETCH), .en(1'b1), .clk(CLK), .Q(O_DONE), .clr(1'b0));
  not not_1 (not_1_out, O_DONE);
  and and_1 (and_1_out, FETCH, not_1_out);
  Register #(.width(24)) register_2 (.D(IROM_L_data), .en(and_1_out), .clk(CLK), .Q(ODATA_L), .clr(1'b0));
  ROM #(.addrWidth(15), .dataWidth(24)) IROM_H (.addr(I_ADDR), .data(IROM_H_data));
  Register #(.width(24)) register_3 (.D(IROM_H_data), .en(and_1_out), .clk(CLK), .Q(ODATA_H), .clr(1'b0));
endmodule

module CPU (
  input  CLK,
  input  RESET,
  input  IRQ,
  input  [23:0] IBUS_IDATA_L,
  input  [23:0] IBUS_IDATA_H,
  input  IBUS_DONE,
  input  [23:0] DBUS_IDATA_L,
  input  [23:0] DBUS_IDATA_H,
  input  DBUS_DONE,
  output IBUS_FETCH,
  output [14:0] IBUS_ADDR,
  output DBUS_READ,
  output DBUS_WRITE,
  output [14:0] DBUS_ADDR,
  output [23:0] DBUS_ODATA_L,
  output [23:0] DBUS_ODATA_H
);

  wire ACC_IS_ZERO, alu_done, and_2_out, and_3_out, and_4_out, and_5_out, and_6_out, and_7_out, and_8_out,
       and_9_out, branch, busy, comparator_1_eq, comparator_2_eq, comparator_3_eq, comparator_6_eq,
       comparator_7_eq, comparator_8_eq, cond_acc_neg, cond_acc_nonzero, cond_acc_zero, cond_op_not_cached,
       decode, enter_interrupt, exit_interrupt, gie, IS_OP_CACHED, Mi_is_zero, multiplexer_1_out, not_1_out,
       not_2_out, not_3_out, not_4_out, not_5_out, not_6_out, not_7_out, not_8_out, not_9_out, not_10_out,
       not_11_out, not_12_out, op_lflag, op_utc0, op_xta0, or_1_out, or_4_out, or_5_out, or_6_out, or_7_out,
       P_C_ACTIVE, P_DECODE, P_ENTER_INT, P_EXIT_INT, P_M_ZERO, P_SEL_ADDR, P_SEL_ALU_MEM, P_W_A, P_W_C,
       P_W_PC, sel_c_mem, w_opcode;
  wire [0:0] PC_Q;
  wire [1:0] P_SEL_MR, P_SEL_MW;
  wire [3:0] bit_extender_1_out, bit_extender_2_out, bit_extender_3_out, bit_extender_4_out,
       bit_extender_5_out, bit_extender_6_out, m_ra, m_wa, reg_index;
  wire [5:0] alu_op, R_Q;
  wire [8:0] adder_1_out, imm, jmp_tbl_1_mc_addr, multiplexer_2_out, multiplexer_3_out, multiplexer_4_out,
       multiplexer_9_out, multiplexer_10_out, upc_next, UPC_q;
  wire [14:0] C_Q, m_bank_1_m0, m_bank_1_m1, m_bank_1_m2, m_bank_1_m3, m_bank_1_m4, m_bank_1_m5, m_bank_1_m6,
       m_bank_1_m7, m_bank_1_m8, m_bank_1_m9, m_bank_1_m10, m_bank_1_m11, m_bank_1_m12, m_bank_1_m13,
       m_bank_1_m14, m_bank_1_m15, Mi, Mr, pc_cached_q, Uaddr, Vaddr;
  wire [23:0] opcode, OPCODE_CACHE_H_q, OPCODE_CACHE_L_q;
  wire [31:3] uop_h;
  wire [31:15] uop_l;

  or or_1 (or_1_out, DBUS_READ, DBUS_WRITE);
  not not_1 (not_1_out, DBUS_DONE);
  not not_2 (not_2_out, IBUS_DONE);
  Comparator #(.width(6)) comparator_1 (.a(alu_op), .b({6{1'b0}}), .eq(comparator_1_eq));  // open: gt, lt
  not not_3 (not_3_out, alu_done);
  not not_4 (not_4_out, busy);
  and and_1 (decode, not_4_out, P_DECODE);
  and and_2 (and_2_out, cond_op_not_cached, not_5_out);
  not not_5 (not_5_out, IS_OP_CACHED);
  and and_3 (and_3_out, cond_acc_zero, ACC_IS_ZERO);
  not not_6 (not_6_out, ACC_IS_ZERO);
  and and_4 (and_4_out, not_6_out, cond_acc_nonzero);
  and and_5 (and_5_out, cond_acc_neg, DBUS_ODATA_H[8]);
  and and_6 (and_6_out, P_M_ZERO, Mi_is_zero);
  Register #(.width(6)) R (.Q(R_Q));  // open: D, en, clk, clr
  and and_7 (and_7_out, or_1_out, not_1_out);
  and and_8 (and_8_out, IBUS_FETCH, not_2_out);
  not not_7 (not_7_out, comparator_1_eq);
  and and_9 (and_9_out, not_7_out, not_3_out);
  Register #(.width(4)) u_reg_index (.Q(reg_index));  // open: D, en, clk, clr
  or or_2 (busy, and_7_out, and_8_out, and_9_out);
  or or_3 (branch, and_2_out, and_3_out, and_4_out, and_5_out, and_6_out, cond_op_not_cached);
  REG_48 ACC (.Q_L(DBUS_ODATA_L), .Q_H(DBUS_ODATA_H));  // open: CLK, WE, D_L, D_H
  Comparator #(.width(24)) comparator_2 (.a(DBUS_ODATA_L), .b({24{1'b0}}), .eq(comparator_2_eq));  // open: gt, lt
  Comparator #(.width(24)) comparator_3 (.a(DBUS_ODATA_H), .b({24{1'b0}}), .eq(comparator_3_eq));  // open: gt, lt
  REG_48 Y (.Q_L(DBUS_ODATA_L), .Q_H(DBUS_ODATA_H));  // open: CLK, WE, D_L, D_H
  JMP_TBL jmp_tbl_1 (.MC_ADDR(jmp_tbl_1_mc_addr));  // open: CMD
  Register #(.width(15)) u_Vaddr (.Q(Vaddr));  // open: D, en, clk, clr
  or or_4 (or_4_out, enter_interrupt, RESET);
  Multiplexer #(.enable("false")) multiplexer_1 (
    .in0(exit_interrupt), .in1(1'b0), .out(multiplexer_1_out), .sel(or_4_out));
  and and_10 (ACC_IS_ZERO, comparator_2_eq, comparator_3_eq);
  or or_5 (or_5_out, op_xta0, op_utc0);
  not not_8 (not_8_out, busy);
  and and_11 (exit_interrupt, not_8_out, P_EXIT_INT);
  not not_9 (not_9_out, busy);
  and and_12 (enter_interrupt, not_9_out, P_ENTER_INT);
  or or_6 (or_6_out, exit_interrupt, or_4_out);
  Register #(.width(1)) u_gie (.D(multiplexer_1_out), .en(or_6_out), .clk(CLK), .Q(gie));  // open: clr
  Multiplexer #(.width(9), .enable("false")) multiplexer_2 (
    .in0(jmp_tbl_1_mc_addr), .in1(9'h16), .out(multiplexer_2_out), .sel(or_5_out));
  M_BANK m_bank_1 (
    .M0(m_bank_1_m0), .M1(m_bank_1_m1), .M2(m_bank_1_m2), .M3(m_bank_1_m3), .M4(m_bank_1_m4),
    .M5(m_bank_1_m5), .M6(m_bank_1_m6), .M7(m_bank_1_m7), .M8(m_bank_1_m8), .M9(m_bank_1_m9),
    .M10(m_bank_1_m10), .M11(m_bank_1_m11), .M12(m_bank_1_m12), .M13(m_bank_1_m13), .M14(m_bank_1_m14),
    .M15(m_bank_1_m15));  // open: CLK, D
  Bit_Extender #(.in_width(9), .out_width(4), .\type ("zero")) bit_extender_1 (.in(imm), .out(bit_extender_1_out));
  Bit_Extender #(.in_width(15), .out_width(4), .\type ("zero")) bit_extender_2 (.in(Vaddr), .out(bit_extender_2_out));
  Bit_Extender #(.in_width(15), .out_width(4), .\type ("zero")) bit_extender_3 (.in(Uaddr), .out(bit_extender_3_out));
  Bit_Extender #(.in_width(9), .out_width(4), .\type ("zero")) bit_extender_4 (.in(imm), .out(bit_extender_4_out));
  Bit_Extender #(.in_width(15), .out_width(4), .\type ("zero")) bit_extender_5 (.in(Vaddr), .out(bit_extender_5_out));
  Bit_Extender #(.in_width(15), .out_width(4), .\type ("zero")) bit_extender_6 (.in(Uaddr), .out(bit_extender_6_out));
  Adder #(.width(9)) adder_1 (.a(9'h1), .b(UPC_q), .out(adder_1_out));  // open: cin, cout
  Multiplexer #(.width(9), .enable("false")) multiplexer_3 (
    .in0(multiplexer_2_out), .in1(9'h17), .out(multiplexer_3_out), .sel(IRQ));
  ALU alu_1 (
    .CLK(CLK), .ALU_OP(alu_op), .ALU_DONE(alu_done));  // open: ALU_A_H, ALU_A_L, ALU_B_H, ALU_B_L, ALU_R_H, ALU_R_L, ALU_Y_H, ALU_Y_L
  Multiplexer #(.width(9), .enable("false")) multiplexer_4 (
    .in0(adder_1_out), .in1(multiplexer_3_out), .out(multiplexer_4_out), .sel(decode));
  Multiplexer #(.select(2), .width(4), .enable("false")) multiplexer_5 (
    .in0(reg_index), .in1(bit_extender_1_out), .in2(bit_extender_2_out), .in3(bit_extender_3_out),
    .out(m_ra), .sel(P_SEL_MR));
  Multiplexer #(.select(2), .width(4), .enable("false")) multiplexer_6 (
    .in0(reg_index), .in1(bit_extender_4_out), .in2(bit_extender_5_out), .in3(bit_extender_6_out),
    .out(m_wa), .sel(P_SEL_MW));
  Multiplexer #(.select(4), .width(15), .enable("false")) multiplexer_7 (
    .in0(m_bank_1_m0), .in1(m_bank_1_m1), .in2(m_bank_1_m2), .in3(m_bank_1_m3), .in4(m_bank_1_m4),
    .in5(m_bank_1_m5), .in6(m_bank_1_m6), .in7(m_bank_1_m7), .in8(m_bank_1_m8), .in9(m_bank_1_m9),
    .in10(m_bank_1_m10), .in11(m_bank_1_m11), .in12(m_bank_1_m12), .in13(m_bank_1_m13), .in14(m_bank_1_m14),
    .in15(m_bank_1_m15), .out(Mi), .sel(reg_index));
  Multiplexer #(.select(4), .width(15), .enable("false")) multiplexer_8 (
    .in0(m_bank_1_m0), .in1(m_bank_1_m1), .in2(m_bank_1_m2), .in3(m_bank_1_m3), .in4(m_bank_1_m4),
    .in5(m_bank_1_m5), .in6(m_bank_1_m6), .in7(m_bank_1_m7), .in8(m_bank_1_m8), .in9(m_bank_1_m9),
    .in10(m_bank_1_m10), .in11(m_bank_1_m11), .in12(m_bank_1_m12), .in13(m_bank_1_m13), .in14(m_bank_1_m14),
    .in15(m_bank_1_m15), .out(Mr), .sel(m_ra));
  Multiplexer #(.width(9), .enable("false")) multiplexer_9 (
    .in0(multiplexer_4_out), .in1(imm), .out(multiplexer_9_out), .sel(branch));
  Comparator #(.width(15)) comparator_4 (.a(Mi), .b({15{1'b0}}), .eq(Mi_is_zero));  // open: gt, lt
  Multiplexer #(.width(9), .enable("false")) multiplexer_10 (
    .in0(multiplexer_9_out), .in1(UPC_q), .out(multiplexer_10_out), .sel(busy));
  Multiplexer #(.width(9), .enable("false")) multiplexer_11 (
    .in0(multiplexer_10_out), .in1({9{1'b0}}), .out(upc_next), .sel(RESET));
  // Probe on upc_next
  Register #(.width(16)) PC (.Q({IBUS_ADDR, PC_Q[0]}));  // open: D, en, clk, clr
  Register #(.width(24)) OPCODE_CACHE_L (
    .D(IBUS_IDATA_L), .en(w_opcode), .clk(CLK), .Q(OPCODE_CACHE_L_q));  // open: clr
  Register #(.width(24)) OPCODE_CACHE_H (
    .D(IBUS_IDATA_H), .en(w_opcode), .clk(CLK), .Q(OPCODE_CACHE_H_q));  // open: clr
  Register #(.width(15)) PC_CACHED (.D(IBUS_ADDR), .en(w_opcode), .clk(CLK), .Q(pc_cached_q));  // open: clr
  Register #(.width(9)) UPC (.D(upc_next), .en(1'b1), .clk(CLK), .Q(UPC_q), .clr(1'b0));
  Comparator #(.width(15)) comparator_5 (.a(pc_cached_q), .b(IBUS_ADDR), .eq(IS_OP_CACHED));  // open: gt, lt
  MC_ROM mc_rom_1 (
    .ADDR(upc_next),
    .UOP_L({uop_l[31], P_SEL_ADDR, uop_l[29:26], P_SEL_MR, uop_l[23], P_SEL_MW, uop_l[20:15], alu_op, imm}),
    .UOP_H({uop_h[31:19], P_SEL_ALU_MEM, P_M_ZERO, P_W_PC, P_EXIT_INT, P_ENTER_INT, P_C_ACTIVE, cond_op_not_cached, cond_acc_zero, cond_acc_neg, cond_acc_nonzero, P_W_C, P_W_A, DBUS_WRITE, DBUS_READ, P_DECODE, uop_h[3], IBUS_FETCH, cond_op_not_cached, sel_c_mem}));
  Multiplexer #(.width(24), .enable("false")) multiplexer_12 (
    .in0(OPCODE_CACHE_H_q), .in1(OPCODE_CACHE_L_q), .out(opcode), .sel(PC_Q[0]));
  Register #(.width(15)) C (.Q(C_Q));  // open: D, en, clk, clr
  Comparator #(.width(24)) comparator_6 (.a(opcode), .b(24'h22000), .eq(comparator_6_eq));  // open: gt, lt
  Comparator #(.width(24)) comparator_7 (.a(opcode), .b(24'h8000), .eq(comparator_7_eq));  // open: gt, lt
  Comparator #(.width(24)) comparator_8 (.a(opcode), .b(24'h90000), .eq(comparator_8_eq));  // open: gt, lt
  OP_SPLITTER op_splitter_1 (.OPCODE(opcode), .OP_LFLAG(op_lflag));  // open: OP_IR, OP_LCMD, OP_SCMD, OP_ADDR
  not not_10 (not_10_out, P_C_ACTIVE);
  or or_7 (or_7_out, comparator_6_eq, comparator_7_eq);
  not not_11 (not_11_out, P_C_ACTIVE);
  and and_13 (op_xta0, not_10_out, or_7_out);
  and and_14 (op_utc0, not_11_out, comparator_8_eq);
  not not_12 (not_12_out, busy);
  and and_15 (w_opcode, not_12_out, uop_h[3]);

  // Other names for the same wires on the sheet: ACC_H[23:0] = DBUS_ODATA_H; ACC_IS_NEG = DBUS_ODATA_H[8];
  //   ACC_L[23:0] = DBUS_ODATA_L; PC_Q[15:1] = IBUS_ADDR;
  //   uop_h (some bits) = {P_SEL_ALU_MEM, P_M_ZERO, P_W_PC, P_EXIT_INT, P_ENTER_INT, P_C_ACTIVE, cond_op_not_cached, cond_acc_zero, cond_acc_neg, cond_acc_nonzero, P_W_C, P_W_A, DBUS_WRITE, DBUS_READ, P_DECODE, IBUS_FETCH, cond_op_not_cached, sel_c_mem};
  //   fetch = IBUS_FETCH; mem_r = DBUS_READ; mem_w = DBUS_WRITE; P_A_NONZERO = cond_acc_nonzero;
  //   P_A_ZERO = cond_acc_zero; op_not_cached = cond_op_not_cached; P_BRANCH = cond_op_not_cached;
  //   uop_l (some bits) = {P_SEL_ADDR, P_SEL_MR, P_SEL_MW, alu_op, imm}

  // Notes on the sheet:
  //   TODO
endmodule

module DRAM (
  input  CLK,
  input  DBUS_READ,
  input  DBUS_WRITE,
  input  [14:0] DBUS_ADDR,
  input  [23:0] DBUS_IDATA_L,
  input  [23:0] DBUS_IDATA_H,
  output DBUS_DONE,
  output [23:0] DBUS_ODATA_L,
  output [23:0] DBUS_ODATA_H
);

  wire comparator_1_eq, comparator_2_eq, or_1_out;
  wire [23:0] multiplexer_1_out, multiplexer_2_out, ram_1_dout, ram_2_dout;

  RAM #(.addrWidth(15), .dataWidth(24), .databus("bibus")) ram_1 (
    .addr(DBUS_ADDR), .we(DBUS_WRITE), .oe(DBUS_READ), .clk(CLK), .din(DBUS_IDATA_L), .dout(ram_1_dout));
  RAM #(.addrWidth(15), .dataWidth(24), .databus("bibus")) ram_2 (
    .addr(DBUS_ADDR), .we(DBUS_WRITE), .oe(DBUS_READ), .clk(CLK), .din(DBUS_IDATA_H), .dout(ram_2_dout));
  Comparator #(.width(15)) comparator_1 (.a(DBUS_ADDR), .b({15{1'b0}}), .eq(comparator_1_eq));  // open: gt, lt
  Comparator #(.width(15)) comparator_2 (.a(DBUS_ADDR), .b({15{1'b0}}), .eq(comparator_2_eq));  // open: gt, lt
  Multiplexer #(.width(24), .enable("false")) multiplexer_1 (
    .in0(ram_1_dout), .in1({24{1'b0}}), .out(multiplexer_1_out), .sel(comparator_1_eq));
  Multiplexer #(.width(24), .enable("false")) multiplexer_2 (
    .in0(ram_2_dout), .in1({24{1'b0}}), .out(multiplexer_2_out), .sel(comparator_2_eq));
  Register #(.width(24)) register_1 (.D(multiplexer_1_out), .en(DBUS_READ), .clk(CLK), .Q(DBUS_ODATA_L), .clr(1'b0));
  Register #(.width(1)) register_2 (.D(or_1_out), .en(1'b1), .clk(CLK), .Q(DBUS_DONE), .clr(1'b0));
  or or_1 (or_1_out, DBUS_WRITE, DBUS_READ);
  Register #(.width(24)) register_3 (.D(multiplexer_2_out), .en(DBUS_READ), .clk(CLK), .Q(DBUS_ODATA_H), .clr(1'b0));
endmodule

module JMP_TBL (
  input  [23:0] CMD,
  output [8:0] MC_ADDR
);

  wire [8:0] rom_1_data, rom_2_data;

  ROM #(.addrWidth(6), .dataWidth(9)) rom_1 (.addr(CMD[17:12]), .data(rom_1_data));
  ROM #(.addrWidth(4), .dataWidth(9)) rom_2 (.addr(CMD[18:15]), .data(rom_2_data));
  Multiplexer #(.width(9), .enable("false")) multiplexer_1 (
    .in0(rom_1_data), .in1(rom_2_data), .out(MC_ADDR), .sel(CMD[19]));

  // Notes on the sheet:
  //   contents of rom_1 (hex, n*v repeats v):
  //   19 1b 1c 1d 1e 1f 20 21 22 24 27 2a 2d 2e 31 32 33 34 35 36 37 38 39 3a 3b 3c 3d 3e 3f 40 41 42 43
  //   45 46 48 49 4a 4b 4c 4d 4e 4f 50 51 52 53 54 55 56 57 58 59 5a 5b 5c 5d 5e 5f 60 61 62 63 64
  //   contents of rom_2 (hex, n*v repeats v):
  //   65 66 67 69 6b 6c 6d 71 75 77 79 7a 7b 7f 83 84
endmodule

module MC_ROM (
  input  [8:0] ADDR,
  output [31:0] UOP_L,
  output [31:0] UOP_H
);

  ROM #(.addrWidth(9), .dataWidth(32)) MC_L (.addr(ADDR), .data(UOP_L));
  ROM #(.addrWidth(9), .dataWidth(32)) MC_H (.addr(ADDR), .data(UOP_H));

  // Notes on the sheet:
  //   contents of MC_L (hex, n*v repeats v):
  //   a40000 1010000 a40001 a40002 a40003 a40004 a40005 a40006 a40007 a40008 a40009 a4000a a4000b a4000c
  //   a4000d a4000e a4000f 18000001 4*0 12 0 12 0 8*12 8000 12 8000 200 12 8000 600 12 8000 a00 12 12 8000
  //   400 19*12 e40012 12 12 3010000 12 12 c80012 82d80012 28*12 0 14 0 14 940012 980012 6f 12 0 12 73 12
  //   0 12 0 12 8800000 12 12 12 7d 12 8000000 12 4000081 12 8000000 12 12 4000086 12 88c0000 12
  //   contents of MC_H (hex, n*v repeats v):
  //   0 80 15*0 18000 c 10 c 2010 12 4000 12 40 8*12 a0 12 20 40080 12 20 40080 12 20 40080 12 12 20 40080
  //   22*12 80 32*12 100 2012 121 2012 12 12 800 12 10000 12 200 12 10000 12 10000 12 10000 12 12 12 20000
  //   12 10000 12 0 12 10000 12 12 0 12 10000 12
endmodule

module REG_48 (
  input  CLK,
  input  WE,
  input  [23:0] D_L,
  input  [23:0] D_H,
  output [23:0] Q_L,
  output [23:0] Q_H
);

  Register #(.width(24)) register_1 (.D(D_L), .en(WE), .clk(CLK), .Q(Q_L), .clr(1'b0));
  Register #(.width(24)) register_2 (.D(D_H), .en(WE), .clk(CLK), .Q(Q_H), .clr(1'b0));
endmodule

module M_BANK (
  input  CLK,
  input  [14:0] D,
  output [14:0] M0,
  output [14:0] M1,
  output [14:0] M2,
  output [14:0] M3,
  output [14:0] M4,
  output [14:0] M5,
  output [14:0] M6,
  output [14:0] M7,
  output [14:0] M8,
  output [14:0] M9,
  output [14:0] M10,
  output [14:0] M11,
  output [14:0] M12,
  output [14:0] M13,
  output [14:0] M14,
  output [14:0] M15
);

  Register #(.width(15)) register_1 (.D(D), .Q(M1));  // open: en, clk, clr
  Register #(.width(15)) register_2 (.D(D), .Q(M2));  // open: en, clk, clr
  Register #(.width(15)) register_3 (.D(D), .Q(M3));  // open: en, clk, clr
  Register #(.width(15)) register_4 (.D(D), .Q(M4));  // open: en, clk, clr
  Register #(.width(15)) register_5 (.D(D), .Q(M5));  // open: en, clk, clr
  Register #(.width(15)) register_6 (.D(D), .Q(M6));  // open: en, clk, clr
  Register #(.width(15)) register_7 (.D(D), .Q(M7));  // open: en, clk, clr
  Register #(.width(15)) register_8 (.D(D), .Q(M8));  // open: en, clk, clr
  Register #(.width(15)) register_9 (.D(D), .Q(M9));  // open: en, clk, clr
  Register #(.width(15)) register_10 (.D(D), .Q(M10));  // open: en, clk, clr
  Register #(.width(15)) register_11 (.D(D), .Q(M11));  // open: en, clk, clr
  Register #(.width(15)) register_12 (.D(D), .Q(M12));  // open: en, clk, clr
  Register #(.width(15)) register_13 (.D(D), .Q(M13));  // open: en, clk, clr
  Register #(.width(15)) register_14 (.D(D), .Q(M14));  // open: en, clk, clr
  Register #(.width(15)) register_15 (.D(D), .Q(M15));  // open: en, clk, clr

  assign M0 = {15{1'b0}};
endmodule

module OP_SPLITTER (
  input  [23:0] OPCODE,
  output OP_LFLAG,
  output [3:0] OP_IR,
  output [3:0] OP_LCMD,
  output [5:0] OP_SCMD,
  output [14:0] OP_ADDR
);

  wire [2:0] bit_extender_2_out;
  wire [14:0] bit_extender_1_out;

  Bit_Extender #(.in_width(24), .out_width(15), .\type ("zero")) bit_extender_1 (.in(OPCODE), .out(bit_extender_1_out));
  assign bit_extender_2_out = {{2{OPCODE[18]}}, OPCODE[18]};  // Bit_Extender bit_extender_2
  Multiplexer #(.width(15), .enable("false")) multiplexer_1 (
    .in0({bit_extender_2_out, OPCODE[11:0]}), .in1(bit_extender_1_out), .out(OP_ADDR), .sel(OPCODE[19]));

  assign OP_IR = OPCODE[23:20];
  assign OP_LCMD = OPCODE[18:15];
  assign OP_LFLAG = OPCODE[19];
  assign OP_SCMD = OPCODE[17:12];
endmodule
